// Logisim project cpu.circ as structural Verilog: 1 circuit, main circuit cpu
module cpu (
  input  clk,
  input  [31:0] INSTRUCTION,
  input  [31:0] READ_DATA,
  output [31:0] WRITE_ADDRESS,
  output [31:0] ProgramCounter,
  output [31:0] ra,
  output [31:0] sp,
  output [31:0] t0,
  output [31:0] t1,
  output [31:0] t2,
  output [31:0] s0,
  output [31:0] s1,
  output [31:0] a0,
  output [3:0] WRITE_ENABLE,
  output [31:0] WRITE_DATA
);

  wire Asel, BrEq, BrLt, BrUn, Bsel, LB, LH, PCSel, RegWEn, SB, SH;
  wire [2:0] ImmSel;
  wire [3:0] ALUSel;
  wire [4:0] ReadIndex1, ReadIndex2, WriteIndex;
  wire [31:0] adder_1_out, ALU_output, Immediate, Instruction_t, multiplexer_1_out, multiplexer_2_out,
       ReadData1, ReadData2, WriteData;

  Adder #(.width(32)) adder_1 (.a(ProgramCounter), .b(32'h4), .out(adder_1_out));  // open: cin, cout
  Register #(.width(32)) PC (.D(adder_1_out), .en(1'b1), .clk(1'b0), .Q(ProgramCounter), .clr(clk));
  // control_logic control_logic_1: pin names not known; wires that end beside it: LB, LH, SB, SH, Instruction_t, PCSel, RegWEn, ImmSel, BrEq, BrLt, BrUn, Asel
  regfile regfile_1 (
    .ReadIndex1(ReadIndex1), .ReadIndex2(ReadIndex2), .WriteIndex(WriteIndex), .WriteData(WriteData),
    .RegWEn(RegWEn), .clk(clk), .ra(ra), .sp(sp), .t0(t0), .t1(t1), .t2(t2), .s0(s0), .s1(s1), .a0(a0));  // open: ReadData1, ReadData2
  imm_gen imm_gen_1 (.inst(Instruction_t), .imm(Immediate));  // open: ImmSel
  Multiplexer #(.width(32)) multiplexer_1 (.in0(ReadData2), .in1(Immediate), .out(multiplexer_1_out), .sel(Bsel));
  Multiplexer #(.width(32)) multiplexer_2 (.in0(ReadData1), .in1({32{1'b0}}), .out(multiplexer_2_out), .sel(Asel));
  // branch_comp branch_comp_1: pin names not known; wires that end beside it: ReadData1, ReadData2, BrUn, 1'b1, BrEq, BrLt
  alu alu_1 (.A(multiplexer_2_out), .B(multiplexer_1_out), .ALUSel(ALUSel), .Result(ALU_output));

  // Other names for the same wires on the sheet: MemAddress[31:0] = WRITE_ADDRESS; MemReadData[31:0] = READ_DATA;
  //   MemWriteData[31:0] = WRITE_DATA; MemWriteMask[3:0] = WRITE_ENABLE

  // Notes on the sheet:
  //   Output to IMEM
  //   IMEM (do **NOT** move this)
  //   Inputs from IMEM
  //   It is OK to move the PC, RegFile, ALU, MEM, Branch Comp, Imm Gen, and Control Logic to wherever is most convenient for you when constructing your CPU, and to delete this text
  //   Inputs/Outputs for testing. Do **NOT** move these.
  //   Outputs To DMEM
  //   DMEM (do **NOT** move this)
  //   Inputs From DMEM
endmodule
